# Fritzing sketch esquema botonera (saved by Fritzing 0.9.3b)
breadboards: 1

parts:
  Componente1 = Arduino Nano (Rev3.0) (ICSP)
  X1 = X113647 Stepper Driver Board [package=board]
  X2 = X113647 Stepper Driver Board [package=board]
  J1 = female pin header, 7 pins [form="♀ (female)"]
  J2 = Piezo Speaker
  VCC1 = Battery

nets:
  GND: Componente1.GND, X1.GND, X2.GND, J1.pin7, J2.pin1, VCC1.-
  N1: Componente1.D2, X2.IN4
  N2: Componente1.D3, X2.IN3
  N3: Componente1.D4, X2.IN2
  N4: Componente1.D5, X2.IN1
  N5: Componente1.D6, X1.IN4
  N6: Componente1.D7, X1.IN3
  N7: Componente1.D8, X1.IN2
  N8: Componente1.D9, X1.IN1
  N9: Componente1.D10, J2.pin2
  N10: Componente1.VIN, X1.+V, X2.+V, VCC1.+
  N11: Componente1.5V, J1.pin5
  N12: Componente1.A7, J1.pin6
  N13: Componente1.A3, J1.pin1
  N14: Componente1.A2, J1.pin2
  N15: Componente1.A1, J1.pin3
  N16: Componente1.A0, J1.pin4

notes:
  Botonera
  L4 L3 L2 L1 5V SIG GND

custom parts:
  X113647 Stepper Driver Board: A common stepper motor driver board based on ULN2003APG darlington array
